// Logisim project 5.circ as structural Verilog: 1 circuit, main circuit main
module main (
);

  wire Control_alu, Control_memtoreg, Control_memwrite, Control_regdst, Control_regwrite, undriven;
  wire [1:0] Control_alu_op, INSTRUCTION_MEMORY_PC_p1, INSTRUCTION_MEMORY_PC_p3, INSTRUCTION_MEMORY_PC_p5,
       INSTRUCTION_MEMORY_PC_p7, multiplexer_1_out;
  wire [3:0] ALU_output, multiplexer_3_out, undriven_2;

  // Q4B3_main INSTRUCTION_MEMORY_PC: pin names not known; wires that end beside it: INSTRUCTION_MEMORY_PC_p1[0], INSTRUCTION_MEMORY_PC_p1[1], INSTRUCTION_MEMORY_PC_p3[0], INSTRUCTION_MEMORY_PC_p3[1], INSTRUCTION_MEMORY_PC_p5[0], INSTRUCTION_MEMORY_PC_p5[1], INSTRUCTION_MEMORY_PC_p7[0], INSTRUCTION_MEMORY_PC_p7[1]
  Multiplexer #(.width(2), .enable("false")) multiplexer_1 (
    .in0(INSTRUCTION_MEMORY_PC_p5), .in1(INSTRUCTION_MEMORY_PC_p7), .out(multiplexer_1_out),
    .sel(Control_regdst));
  Multiplexer #(.width(4), .enable("false")) multiplexer_2 (
    .in0(ALU_output), .in1(undriven_2), .sel(Control_memtoreg));  // open: out
  ControlTruth Control (
    .OpCode(INSTRUCTION_MEMORY_PC_p1), .RegDst(Control_regdst), .ALU(Control_alu),
    .MemtoReg(Control_memtoreg), .RegWrite(Control_regwrite), .MemWrite(Control_memwrite),
    .ALU_OP(Control_alu_op));  // open: MemRead
  ALU ALU (
    .Input2(multiplexer_3_out), .ControlBits(Control_alu_op), .Output(ALU_output));  // open: Input1, CarryOut, Zero
  Multiplexer #(.width(4), .enable("false")) multiplexer_3 (
    .in1({INSTRUCTION_MEMORY_PC_p7, 2'b00}), .out(multiplexer_3_out), .sel(Control_alu));  // open: in0
  Diarmuid_Ryan_11363776_A4_main DATA_MEM_REG (
    .RegWrite(multiplexer_1_out), .RegWrite_2(Control_regwrite), .MemAdd(ALU_output), .MemWrite(undriven),
    .ExtDataWrite(Control_memwrite), .ExtData(undriven_2));  // open: RegRead1, RegRead2, CLK

  // Notes on the sheet:
  //   OP
  //   RS
  //   RT
  //   RD/Offset
endmodule
